// Logisim project S1-T7.circ as structural Verilog: 2 circuits, main circuit main
module main (
  input  in_1,
  input  [3:0] in_2,
  input  in_3,
  input  [3:0] B,
  input  in_5,
  input  [3:0] in_6,
  input  in_7,
  input  [3:0] D,
  input  _0,
  input  _1,
  input  _2,
  input  [3:0] in_12,
  input  _3,
  input  _4,
  input  _5,
  input  _6,
  input  _7,
  input  _8,
  input  _9,
  input  _0_2,
  input  _1_2,
  input  _2_2,
  input  [3:0] in_23,
  input  _3_2,
  input  _4_2,
  input  _5_2,
  input  _6_2,
  input  _7_2,
  input  _8_2,
  input  _9_2,
  input  _0_3,
  input  _1_3,
  input  _2_3,
  input  [3:0] in_34,
  input  _3_3,
  input  _4_3,
  input  _5_3,
  input  _6_3,
  input  _7_3,
  input  _8_3,
  input  _9_3,
  input  _0_4,
  input  _1_4,
  input  _2_4,
  input  [3:0] in_45,
  input  _3_4,
  input  _4_4,
  input  _5_4,
  input  _6_4,
  input  _7_4,
  input  _8_4,
  input  _9_4,
  output [3:0] out_53,
  output out_54,
  output A,
  output [3:0] out_56,
  output B_2,
  output out_58,
  output [3:0] out_59,
  output C,
  output out_61,
  output D_2,
  output [3:0] out_63,
  output out_64,
  output [3:0] out_65,
  output out_66,
  output [3:0] out_67,
  output [3:0] out_68,
  output [3:0] out_69
);

  wire and_1_out, and_2_out, button_1_out, button_2_out, button_3_out, button_4_out, button_5_out,
       button_6_out, comparator_1_eq, comparator_1_gt, comparator_1_lt, comparator_2_eq, comparator_2_gt,
       comparator_2_lt, comparator_3_eq, comparator_3_gt, comparator_3_lt, comparator_4_eq, comparator_4_gt,
       comparator_4_lt, comparator_5_eq, comparator_5_gt, comparator_5_lt, comparator_6_eq, comparator_6_gt,
       comparator_6_lt, display_1_a_2, display_1_b_2, display_1_c_2, display_1_d_2, display_1_e, display_1_f,
       display_1_g, display_2_a_2, display_2_b_2, display_2_c_2, display_2_d_2, display_2_e, display_2_f,
       display_2_g, display_3_a_2, display_3_b_2, display_3_c_2, display_3_d_2, display_3_e, display_3_f,
       display_3_g, display_4_a_2, display_4_b_2, display_4_c_2, display_4_d_2, display_4_e, display_4_f,
       display_4_g, not_1_out, not_2_out, not_3_out, not_4_out, not_5_out, not_6_out, not_7_out, not_8_out,
       not_9_out, or_1_out, or_2_out, or_3_out, or_4_out, or_5_out, or_6_out, or_7_out, or_8_out, or_9_out,
       or_10_out, or_11_out, or_12_out, or_13_out, or_14_out, or_15_out, or_16_out, or_17_out;
  wire [3:0] xor_1_out, xor_2_out, xor_3_out, xor_4_out;

  Button button_1 (.out(button_1_out));
  and and_1 (and_1_out, not_1_out, not_2_out, not_3_out, not_4_out);
  not not_1 (not_1_out, out_54);
  not not_2 (not_2_out, out_58);
  not not_3 (not_3_out, out_61);
  not not_4 (not_4_out, out_64);
  Register #(.width(1)) register_1 (.D(1'b1), .en(1'b1), .Q(out_54), .clk(button_3_out), .clr(button_2_out));
  Register #(.width(1)) register_2 (.D(1'b1), .en(1'b1), .Q(out_58), .clk(button_4_out), .clr(button_2_out));
  Register #(.width(1)) register_3 (.D(1'b1), .en(1'b1), .Q(out_61), .clk(button_5_out), .clr(button_2_out));
  Register #(.width(1)) register_4 (.D(1'b1), .en(1'b1), .Q(out_64), .clk(button_6_out), .clr(button_2_out));
  Button button_2 (.out(button_2_out));
  or or_1 (or_1_out, out_54, out_58, out_61, out_64);
  not not_5 (not_5_out, or_1_out);
  display display_1 (
    .A(out_53[3]), .B(out_53[2]), .C(out_53[1]), .D(out_53[0]), .a_2(display_1_a_2), .b_2(display_1_b_2),
    .c_2(display_1_c_2), .d_2(display_1_d_2), .e(display_1_e), .f(display_1_f), .g(display_1_g));
  display display_2 (
    .A(out_56[3]), .B(out_56[2]), .C(out_56[1]), .D(out_56[0]), .a_2(display_2_a_2), .b_2(display_2_b_2),
    .c_2(display_2_c_2), .d_2(display_2_d_2), .e(display_2_e), .f(display_2_f), .g(display_2_g));
  display display_3 (
    .A(out_59[3]), .B(out_59[2]), .C(out_59[1]), .D(out_59[0]), .a_2(display_3_a_2), .b_2(display_3_b_2),
    .c_2(display_3_c_2), .d_2(display_3_d_2), .e(display_3_e), .f(display_3_f), .g(display_3_g));
  display display_4 (
    .A(out_63[3]), .B(out_63[2]), .C(out_63[1]), .D(out_63[0]), .a_2(display_4_a_2), .b_2(display_4_b_2),
    .c_2(display_4_c_2), .d_2(display_4_d_2), .e(display_4_e), .f(display_4_f), .g(display_4_g));
  _7_Segment_Display u_7_segment_display_1 (
    .g(display_1_g), .f(display_1_f), .a(display_1_a_2), .b(display_1_b_2), .e(display_1_e),
    .d(display_1_d_2), .c(display_1_c_2));  // open: dp
  _7_Segment_Display u_7_segment_display_2 (
    .g(display_2_g), .f(display_2_f), .a(display_2_a_2), .b(display_2_b_2), .e(display_2_e),
    .d(display_2_d_2), .c(display_2_c_2));  // open: dp
  _7_Segment_Display u_7_segment_display_3 (
    .g(display_3_g), .f(display_3_f), .a(display_3_a_2), .b(display_3_b_2), .e(display_3_e),
    .d(display_3_d_2), .c(display_3_c_2));  // open: dp
  _7_Segment_Display u_7_segment_display_4 (
    .g(display_4_g), .f(display_4_f), .a(display_4_a_2), .b(display_4_b_2), .e(display_4_e),
    .d(display_4_d_2), .c(display_4_c_2));  // open: dp
  and and_2 (and_2_out, and_1_out, out_66);
  Button button_3 (.out(button_3_out));
  Button button_4 (.out(button_4_out));
  Button button_5 (.out(button_5_out));
  Button button_6 (.out(button_6_out));
  Priority_Encoder #(.select(4)) priority_encoder_1 (
    .in0(_0), .in1(_1), .in2(_2), .in3(_3), .in4(_4), .in5(_5), .in6(_6), .in7(_7), .in8(_8), .in9(_9),
    .out(out_65), .en_in(not_5_out));  // open: in10, in11, in12, in13, in14, in15, gs, en_out
  Priority_Encoder #(.select(4)) priority_encoder_2 (
    .in0(_0_2), .in1(_1_2), .in2(_2_2), .in3(_3_2), .in4(_4_2), .in5(_5_2), .in6(_6_2), .in7(_7_2),
    .in8(_8_2), .in9(_9_2), .out(out_67), .en_in(not_5_out));  // open: in10, in11, in12, in13, in14, in15, gs, en_out
  Priority_Encoder #(.select(4)) priority_encoder_3 (
    .in0(_0_3), .in1(_1_3), .in2(_2_3), .in3(_3_3), .in4(_4_3), .in5(_5_3), .in6(_6_3), .in7(_7_3),
    .in8(_8_3), .in9(_9_3), .out(out_68), .en_in(not_5_out));  // open: in10, in11, in12, in13, in14, in15, gs, en_out
  Priority_Encoder #(.select(4)) priority_encoder_4 (
    .in0(_0_4), .in1(_1_4), .in2(_2_4), .in3(_3_4), .in4(_4_4), .in5(_5_4), .in6(_6_4), .in7(_7_4),
    .in8(_8_4), .in9(_9_4), .out(out_69), .en_in(not_5_out));  // open: in10, in11, in12, in13, in14, in15, gs, en_out
  Counter #(.width(4), .max('hf)) counter_1 (
    .load(in_1), .D(in_2), .count(and_2_out), .Q(out_53), .clk(button_3_out), .clr(button_1_out));  // open: carry
  Counter #(.width(4), .max('hf)) counter_2 (
    .load(in_3), .D(B), .count(and_2_out), .Q(out_56), .clk(button_4_out), .clr(button_1_out));  // open: carry
  Counter #(.width(4), .max('hf)) counter_3 (
    .load(in_5), .D(in_6), .count(and_2_out), .Q(out_59), .clk(button_5_out), .clr(button_1_out));  // open: carry
  Counter #(.width(4), .max('hf)) counter_4 (
    .load(in_7), .D(D), .count(and_2_out), .Q(out_63), .clk(button_6_out), .clr(button_1_out));  // open: carry
  assign xor_1_out = in_12 ^ out_65;  // XOR_Gate xor_1, 4 bits wide
  assign xor_2_out = in_23 ^ out_67;  // XOR_Gate xor_2, 4 bits wide
  assign xor_3_out = in_34 ^ out_68;  // XOR_Gate xor_3, 4 bits wide
  assign xor_4_out = in_45 ^ out_69;  // XOR_Gate xor_4, 4 bits wide
  Comparator #(.width(4), .mode("unsigned")) comparator_1 (
    .a(out_53), .b(out_56), .gt(comparator_1_gt), .eq(comparator_1_eq), .lt(comparator_1_lt));
  Comparator #(.width(4), .mode("unsigned")) comparator_2 (
    .a(out_56), .b(out_59), .gt(comparator_2_gt), .eq(comparator_2_eq), .lt(comparator_2_lt));
  Comparator #(.width(4), .mode("unsigned")) comparator_3 (
    .a(out_59), .b(out_63), .gt(comparator_3_gt), .eq(comparator_3_eq), .lt(comparator_3_lt));
  Comparator #(.width(4), .mode("unsigned")) comparator_4 (
    .a(out_53), .b(out_63), .gt(comparator_4_gt), .eq(comparator_4_eq), .lt(comparator_4_lt));
  Comparator #(.width(4), .mode("unsigned")) comparator_5 (
    .a(out_56), .b(out_63), .gt(comparator_5_gt), .eq(comparator_5_eq), .lt(comparator_5_lt));
  Comparator #(.width(4), .mode("unsigned")) comparator_6 (
    .a(out_53), .b(out_59), .gt(comparator_6_gt), .eq(comparator_6_eq), .lt(comparator_6_lt));
  or or_2 (or_2_out, xor_1_out[0], xor_1_out[1], xor_1_out[2], xor_1_out[3]);
  or or_3 (or_3_out, xor_2_out[0], xor_2_out[1], xor_2_out[2], xor_2_out[3]);
  or or_4 (or_4_out, xor_3_out[0], xor_3_out[1], xor_3_out[2], xor_3_out[3]);
  or or_5 (or_5_out, xor_4_out[0], xor_4_out[1], xor_4_out[2], xor_4_out[3]);
  or or_6 (or_6_out, comparator_1_gt, comparator_1_eq);
  or or_7 (or_7_out, comparator_1_eq, comparator_1_lt);
  or or_8 (or_8_out, comparator_2_gt, comparator_2_eq);
  or or_9 (or_9_out, comparator_2_eq, comparator_2_lt);
  or or_10 (or_10_out, comparator_3_gt, comparator_3_eq);
  or or_11 (or_11_out, comparator_3_eq, comparator_3_lt);
  or or_12 (or_12_out, comparator_4_gt, comparator_4_eq);
  or or_13 (or_13_out, comparator_4_eq, comparator_4_lt);
  or or_14 (or_14_out, comparator_5_gt, comparator_5_eq);
  or or_15 (or_15_out, comparator_5_eq, comparator_5_lt);
  or or_16 (or_16_out, comparator_6_gt, comparator_6_eq);
  or or_17 (or_17_out, comparator_6_eq, comparator_6_lt);
  not not_6 (not_6_out, or_2_out);
  not not_7 (not_7_out, or_3_out);
  not not_8 (not_8_out, or_4_out);
  not not_9 (not_9_out, or_5_out);
  and and_3 (out_66, not_6_out, not_7_out, not_8_out, not_9_out);
  and and_4 (A, or_6_out, or_16_out, or_12_out);
  and and_5 (B_2, or_7_out, or_8_out, or_14_out);
  and and_6 (C, or_9_out, or_10_out, or_17_out);
  and and_7 (D_2, or_11_out, or_13_out, or_15_out);
  LED led_1 (.in(out_66));

  // Notes on the sheet:
  //   TEAM 7
  //   221CS118                        C.GNANA JYOTHI 
  //   221CS139                               P.HASITHA
  //   221CS156                               S.STHUTHI
  //   RESET
  //   PRESS TO ENTER 
  //   PASSWORD
  //   VOTING COUNTER
  //   CAST YOUR VOTE HERE
  //   A
  //   C
  //   ENTER YOUR PASSWORD HERE
  //   SECURE VOTE
  //   A B
  //   B C
  //   C D
  //   BD
  //   AC
  //   U
  //   V
  //   W
  //   A D
  //   X
  //   Y
  //   Z
  //   GREEN-PASSWORD MATCH
  //   RED-PASSWORD MISMATCH
  //   WINNER
endmodule

module display (
  input  A,
  input  B,
  input  C,
  input  D,
  output a_2,
  output b_2,
  output c_2,
  output d_2,
  output e,
  output f,
  output g
);

  wire and_1_out, and_2_out, and_3_out, and_4_out, and_5_out, and_6_out, and_7_out, and_8_out, and_9_out,
       and_10_out, and_11_out, and_12_out, and_13_out, and_14_out, and_15_out, and_16_out, not_1_out,
       not_2_out, not_3_out, not_4_out, not_5_out, not_6_out, not_7_out, not_8_out, not_9_out, not_10_out,
       not_11_out, not_12_out, not_13_out, not_14_out, not_15_out, not_16_out, not_17_out, not_18_out,
       not_19_out, not_20_out, not_21_out;

  not not_1 (not_1_out, B);
  not not_2 (not_2_out, D);
  not not_3 (not_3_out, C);
  not not_4 (not_4_out, D);
  not not_5 (not_5_out, C);
  not not_6 (not_6_out, B);
  not not_7 (not_7_out, D);
  not not_8 (not_8_out, B);
  not not_9 (not_9_out, D);
  not not_10 (not_10_out, C);
  not not_11 (not_11_out, B);
  not not_12 (not_12_out, D);
  not not_13 (not_13_out, D);
  not not_14 (not_14_out, C);
  not not_15 (not_15_out, D);
  not not_16 (not_16_out, C);
  not not_17 (not_17_out, D);
  not not_18 (not_18_out, B);
  not not_19 (not_19_out, C);
  not not_20 (not_20_out, D);
  and and_1 (and_1_out, not_1_out, not_2_out);
  and and_2 (and_2_out, B, D);
  not not_21 (not_21_out, B);
  and and_3 (and_3_out, not_3_out, not_4_out);
  and and_4 (and_4_out, C, D);
  or or_1 (c_2, not_5_out, D, B);
  and and_5 (and_5_out, not_6_out, not_7_out);
  and and_6 (and_6_out, not_8_out, C);
  and and_7 (and_7_out, C, not_9_out);
  and and_8 (and_8_out, B, not_10_out, D);
  and and_9 (and_9_out, not_11_out, not_12_out);
  and and_10 (and_10_out, C, not_13_out);
  and and_11 (and_11_out, not_14_out, not_15_out);
  and and_12 (and_12_out, B, not_16_out);
  and and_13 (and_13_out, B, not_17_out);
  and and_14 (and_14_out, not_18_out, C);
  and and_15 (and_15_out, B, not_19_out);
  and and_16 (and_16_out, B, not_20_out);
  or or_2 (a_2, and_1_out, C, and_2_out, A);
  or or_3 (b_2, not_21_out, and_3_out, and_4_out);
  or or_4 (d_2, and_5_out, and_6_out, and_7_out, and_8_out, A);
  or or_5 (e, and_9_out, and_10_out);
  or or_6 (f, and_11_out, and_12_out, and_13_out, A);
  or or_7 (g, and_14_out, and_15_out, and_16_out, A);

  // Notes on the sheet:
  //   7-SEGMENT DISPLAY
endmodule
